// Digital circuit jelly-seven-loops.dig as structural Verilog
module jelly_seven_loops (
  input  \begin ,
  input  again,
  input  zero,
  input  mode,
  input  move,
  input  D0,
  input  D1,
  input  D2,
  input  D3,
  input  D4,
  input  D5,
  input  D6,
  input  D7,
  input  move_4,
  input  k0,
  input  k1,
  output move_2,
  output move_3,
  output zero_2,
  output FW_BK,
  output A10,
  output CLR,
  output CLR_2
);

  wire and_1_out, and_2_out, and_3_out, and_4_out, and_5_out, and_6_out, and_7_out, d_ff_1_nq, d_ff_2_nq,
       nand_1_out, nand_2_out, or_1_out, or_2_out, or_3_out, or_4_out, or_5_out, or_6_out, or_8_out, or_9_out;

  or or_1 (or_1_out, D0, D1);
  or or_2 (or_2_out, D2, D3);
  or or_3 (or_3_out, D4, D5);
  or or_4 (or_4_out, D6, D7);
  and and_1 (and_1_out, move_4, k0);
  nand nand_1 (nand_1_out, zero, zero);
  nand nand_2 (nand_2_out, mode, mode);
  or or_5 (or_5_out, or_1_out, or_2_out);
  or or_6 (or_6_out, or_3_out, or_4_out);
  xor xor_1 (FW_BK, and_1_out, k1);
  and and_2 (and_2_out, \begin , nand_1_out);
  and and_3 (and_3_out, again, zero);
  and and_4 (and_4_out, nand_1_out, mode);
  and and_5 (and_5_out, mode, move);
  or or_7 (zero_2, or_5_out, or_6_out);
  and and_6 (and_6_out, and_2_out, nand_2_out);
  and and_7 (and_7_out, and_3_out, nand_2_out);
  or or_8 (or_8_out, and_6_out, and_7_out);
  or or_9 (or_9_out, and_7_out, and_5_out);
  or or_10 (CLR, or_8_out, and_4_out);
  nand nand_3 (CLR_2, CLR, CLR);
  D_FF d_ff_1 (.D(d_ff_1_nq), .C(CLR), .Q(A10), .nQ(d_ff_1_nq));
  D_FF d_ff_2 (.D(d_ff_2_nq), .C(or_9_out), .Q(move_3), .nQ(d_ff_2_nq));

  assign move_2 = A10;
endmodule
