// Digital circuit jelly-seven.dig as structural Verilog
module jelly_seven (
  input  clock,
  input  halt,
  input  [7:0] D0,
  input  D1,
  input  D2,
  input  D3,
  input  D4,
  input  D5,
  input  D6,
  input  D7,
  input  MR8,
  input  CLK,
  output D0_2,
  output D1_2,
  output D2_2,
  output D3_2,
  output D4_2,
  output D5_2,
  output D6_2,
  output D7_2,
  output zero,
  output A0,
  output A1,
  output A2,
  output A3,
  output A4,
  output A5,
  output A6,
  output A7,
  output \begin ,
  output again
);

  wire not_1_out, U4_p14, U4_p15, U4_p18, U7_pin12, U7_pin13, U7_pin14, U7_pin15, U7_pin16, U7_pin17,
       U7_pin18, U7_pin19, u8_2_pin3, u8_2_pin6, u8_2_pin8, u8_2_pin13, U8_pin10, u9_pin3, u9_pin6,
       U10_pin11, U10_pin12, U10_pin13, U10_pin14, U10_pin15, U10_pin16, U10_pin17, U10_pin18, U11_pin12,
       U11_pin13;
  wire [2:0] U1_p13, U3_p12, U5_p9, U5_p18, U11_pin14;
  wire [5:3] U8_pin11;
  wire [7:0] U4_p9, U6_pin3, U6_pin12, U8_pin12, U11_pin3;
  wire [7:3] U5_p20, U7_pin5, U11_pin11;
  wire [7:7] U1_p1;

  LED led_1 (.in(D0[0]));
  PullDown pulldown_1 (.out(D0[0]));
  LED led_2 (.in(D0[2]));
  LED led_3 (.in(D0[1]));
  PullDown pulldown_2 (.out(D0[1]));
  PullDown pulldown_3 (.out(D0[2]));
  LED led_4 (.in(D0[4]));
  LED led_5 (.in(D0[3]));
  PullDown pulldown_4 (.out(D0[3]));
  PullDown pulldown_5 (.out(D0[4]));
  LED led_6 (.in(D0[6]));
  LED led_7 (.in(D0[5]));
  PullDown pulldown_6 (.out(D0[5]));
  PullDown pulldown_7 (.out(D0[6]));
  LED led_8 (.in(D0[7]));
  PullDown pulldown_8 (.out(D0[7]));
  _74273 U6 (
    .pin1(U11_pin14[0]), .pin2(U6_pin12[0]), .pin3(U6_pin3[0]), .pin4(U6_pin3[1]), .pin5(U6_pin12[1]),
    .pin6(U6_pin12[2]), .pin7(U6_pin3[2]), .pin8(U6_pin3[3]), .pin9(U6_pin12[3]), .pin10(1'b0),
    .pin11(U11_pin14[1]), .pin12(U6_pin12[4]), .pin13(U6_pin3[4]), .pin14(U6_pin3[5]), .pin15(U6_pin12[5]),
    .pin16(U6_pin12[6]), .pin17(U6_pin3[6]), .pin18(U6_pin3[7]), .pin19(U6_pin12[7]), .pin20(1'b1));
  _74193 U11 (
    .pin1(U6_pin3[1]), .pin2(U11_pin3[1]), .pin3(U11_pin3[0]), .pin4(1'b0), .pin5(CLK), .pin6(U11_pin3[2]),
    .pin7(U11_pin3[3]), .pin8(1'b0), .pin9(U6_pin3[3]), .pin10(U6_pin3[2]), .pin11(U11_pin11[3]),
    .pin12(U11_pin12), .pin13(U11_pin13), .pin14(U11_pin14[2]), .pin15(U6_pin3[0]), .pin16(1'b1));
  _74193 U12 (
    .pin1(U6_pin3[5]), .pin2(U11_pin3[5]), .pin3(U11_pin3[4]), .pin4(U11_pin13), .pin5(U11_pin12),
    .pin6(U11_pin3[6]), .pin7(U11_pin3[7]), .pin8(1'b0), .pin9(U6_pin3[7]), .pin10(U6_pin3[6]),
    .pin11(U11_pin11[3]), .pin14(U11_pin14[2]), .pin15(U6_pin3[4]), .pin16(1'b1));  // open: pin12, pin13
  // _28c16 U4: pin names not known; wires that end beside it: U6_pin12[7], U6_pin12[6], U6_pin12[5], U6_pin12[4], U6_pin12[3], U6_pin12[2], U6_pin12[1], U6_pin12[0], U4_p9[0], U4_p9[1], U4_p9[2], 1'b0, 1'b1, U4_p14, U4_p15, 1'b1, 1'b0, U4_p18, 1'b0, U4_p9[7], U4_p9[6], U4_p9[5]
  _74273 U8 (
    .pin1(MR8), .pin2(U8_pin12[0]), .pin3(U6_pin3[0]), .pin4(U6_pin3[1]), .pin5(U8_pin12[1]),
    .pin6(U8_pin12[2]), .pin7(U6_pin3[2]), .pin8(U6_pin3[3]), .pin9(U8_pin12[3]), .pin10(U8_pin10),
    .pin11(U8_pin11[3]), .pin12(U8_pin12[4]), .pin13(U6_pin3[4]), .pin14(U6_pin3[5]), .pin15(U8_pin12[5]),
    .pin16(U8_pin12[6]), .pin17(U6_pin3[6]), .pin18(U6_pin3[7]), .pin19(U8_pin12[7]), .pin20(1'b1));
  _7432 u8_2 (
    .pin1(U6_pin3[0]), .pin2(U6_pin3[1]), .pin3(u8_2_pin3), .pin4(U6_pin3[2]), .pin5(U6_pin3[3]),
    .pin6(u8_2_pin6), .pin7(1'b0), .pin8(u8_2_pin8), .pin9(u8_2_pin6), .pin10(u8_2_pin3), .pin11(zero),
    .pin12(u8_2_pin8), .pin13(u8_2_pin13), .pin14(1'b1));
  _7432 u9 (
    .pin1(U6_pin3[4]), .pin2(U6_pin3[5]), .pin3(u9_pin3), .pin4(U6_pin3[6]), .pin5(U6_pin3[7]),
    .pin6(u9_pin6), .pin7(1'b0), .pin8(u8_2_pin13), .pin9(u9_pin6), .pin10(u9_pin3), .pin12(1'b1),
    .pin13(1'b1), .pin14(1'b1));  // open: pin11
  LED led_9 (.in(zero));
  LED led_10 (.in(A1));
  LED led_11 (.in(A0));
  PullDown pulldown_9 (.out(A0));
  PullDown pulldown_10 (.out(A1));
  LED led_12 (.in(A3));
  LED led_13 (.in(A2));
  PullDown pulldown_11 (.out(A2));
  PullDown pulldown_12 (.out(A3));
  LED led_14 (.in(A5));
  LED led_15 (.in(A4));
  PullDown pulldown_13 (.out(A4));
  PullDown pulldown_14 (.out(A5));
  // _28c16 U5: pin names not known; wires that end beside it: U8_pin12[7], U8_pin12[6], U8_pin12[5], U8_pin12[4], U8_pin12[3], U8_pin12[2], U8_pin12[1], U8_pin12[0], U5_p9[0], U5_p9[1], U5_p9[2], U8_pin10, 1'b1, U5_p18[0], U5_p18[1], 1'b1, U8_pin10, U5_p18[2], U8_pin10, U5_p20[7], U5_p20[6], U5_p20[5]
  LED led_16 (.in(A7));
  LED led_17 (.in(A6));
  PullDown pulldown_15 (.out(A6));
  PullDown pulldown_16 (.out(A7));
  _74574 U9_2 (
    .pin1(U8_pin11[5]), .pin2(U5_p9[0]), .pin3(U5_p9[1]), .pin4(U5_p9[2]), .pin5(U5_p20[3]),
    .pin6(U5_p20[4]), .pin7(U5_p20[5]), .pin8(U5_p20[6]), .pin9(U5_p20[7]), .pin10(U8_pin10), .pin11(1'b0),
    .pin12(U6_pin3[7]), .pin13(U6_pin3[6]), .pin14(U6_pin3[5]), .pin15(U6_pin3[4]), .pin16(U6_pin3[3]),
    .pin17(U6_pin3[2]), .pin18(U6_pin3[1]), .pin19(U6_pin3[0]), .pin20(1'b1));
  // _28c16 U1: pin names not known; wires that end beside it: U1_p1[7], U4_p9[2], U4_p9[1], U4_p9[0], U11_pin3[3], U11_pin3[2], U11_pin3[1], U11_pin3[0], U11_pin14[0], U11_pin14[1], U11_pin14[2], 1'b1, U1_p13[0], U1_p13[1], 1'b1, 1'b0, U1_p13[2], 1'b0, U11_pin11[7], U11_pin11[6], U11_pin11[5]
  // _28c16 U2: pin names not known; wires that end beside it: 1'b0, U1_p1[7], U4_p9[2], U4_p9[1], U4_p9[0], U11_pin3[3], U11_pin3[2], U11_pin3[1], U11_pin3[0], U5_p18[0], U5_p18[1], U5_p18[2], 1'b1, U1_p13[0], U1_p13[1], 1'b1, 1'b0, U1_p13[2], 1'b0, again, \begin , U8_pin11[5]
  // _28c16 U3: pin names not known; wires that end beside it: 1'b0, U1_p1[7], U4_p9[2], U4_p9[1], U4_p9[0], U11_pin3[3], U11_pin3[2], U11_pin3[1], U11_pin3[0], U3_p12[0], U3_p12[1], U3_p12[2], 1'b0, 1'b1, U1_p13[0], U1_p13[1], 1'b1, 1'b0, U1_p13[2], 1'b0, U7_pin5[7], U7_pin5[6], U7_pin5[5]
  LED led_18 (.in(U6_pin3[0]));
  PullDown pulldown_17 (.out(U6_pin3[0]));
  LED led_19 (.in(U6_pin3[2]));
  LED led_20 (.in(U6_pin3[1]));
  PullDown pulldown_18 (.out(U6_pin3[1]));
  PullDown pulldown_19 (.out(U6_pin3[2]));
  LED led_21 (.in(U6_pin3[4]));
  LED led_22 (.in(U6_pin3[3]));
  PullDown pulldown_20 (.out(U6_pin3[3]));
  PullDown pulldown_21 (.out(U6_pin3[4]));
  LED led_23 (.in(U6_pin3[6]));
  LED led_24 (.in(U6_pin3[5]));
  PullDown pulldown_22 (.out(U6_pin3[5]));
  PullDown pulldown_23 (.out(U6_pin3[6]));
  LED led_25 (.in(U6_pin3[7]));
  PullDown pulldown_24 (.out(U6_pin3[7]));
  _74574 U7 (
    .pin1(U11_pin11[5]), .pin2(U3_p12[0]), .pin3(U3_p12[1]), .pin4(U3_p12[2]), .pin5(U7_pin5[3]),
    .pin6(U7_pin5[4]), .pin7(U7_pin5[5]), .pin8(U7_pin5[6]), .pin9(U7_pin5[7]), .pin10(1'b0),
    .pin11(U11_pin11[4]), .pin12(U7_pin12), .pin13(U7_pin13), .pin14(U7_pin14), .pin15(U7_pin15),
    .pin16(U7_pin16), .pin17(U7_pin17), .pin18(U7_pin18), .pin19(U7_pin19), .pin20(1'b1));
  _74245 U10 (
    .pin1(U11_pin11[7]), .pin2(U6_pin3[0]), .pin3(U6_pin3[1]), .pin4(U6_pin3[2]), .pin5(U6_pin3[3]),
    .pin6(U6_pin3[4]), .pin7(U6_pin3[5]), .pin8(U6_pin3[6]), .pin9(U6_pin3[7]), .pin10(1'b0),
    .pin11(U10_pin11), .pin12(U10_pin12), .pin13(U10_pin13), .pin14(U10_pin14), .pin15(U10_pin15),
    .pin16(U10_pin16), .pin17(U10_pin17), .pin18(U10_pin18), .pin19(U11_pin11[6]), .pin20(1'b1));
  LED led_26 (.in(clock));
  not not_1 (not_1_out, halt);
  LED led_27 (.in(not_1_out));
  // And and_1 has open pins: In_1=clock, In_2=not_1_out, out=open
  // Pins of 1 and 8 bits meet at D0

  assign D0_2 = D0[0];
  assign D1_2 = D0[1];
  assign D2_2 = D0[2];
  assign D3_2 = D0[3];
  assign D4_2 = D0[4];
  assign D5_2 = D0[5];
  assign D6_2 = D0[6];
  assign D7_2 = D0[7];

  // Notes on the sheet:
  //   Data Bus
  //   pipeline counter
  //   Zero detector
  //   opcode counter
  //   Address Bus
  //   tape control eeprom
  //   FSM Bus
  //   Decoder eeprom, translate a byte from ASCII into a valid BF instruction, ignores non valid;
  //   Code control eeprom, does  control logic of finite states for execute the current instruction;
  //   Tape control eeprom, selects which tape is active for use the Data bus and defines modes;
  //   Math operator eeprom, perform all math operations as table lookups;
  //   Basic Logic Level,
  //   check for fail states,
  //   does hold for swap tapes
  //   does hold for move direction
  //   could halt
  //   Data Bus is shared by all tapes
endmodule
