// Digital circuit jelly-two-halt.dig as structural Verilog
module jelly_two_halt (
  input  rd,
  input  wr,
  input  fw,
  input  bk,
  input  bob,
  input  one,
  input  two,
  input  swap,
  output halt,
  output BOB_2,
  output bob_one_two,
  output bob_one,
  output bob_two,
  output one_two,
  output ONE_2,
  output TWO_2
);

  wire and_1_out, and_5_out, and_6_out, and_7_out, and_8_out, and_9_out, and_10_out, d_ff_1_q, nand_1_out,
       or_1_out, or_2_out, or_3_out, or_4_out, or_5_out, or_6_out, or_7_out, or_8_out, xor_1_out, xor_2_out,
       xor_3_out, xor_4_out;

  xor xor_1 (xor_1_out, d_ff_1_q, 1'b1);
  xor xor_2 (xor_2_out, one, two);
  xor xor_3 (xor_3_out, and_1_out, one);
  xor xor_4 (xor_4_out, and_1_out, two);
  D_FF d_ff_1 (.D(xor_1_out), .C(swap), .Q(d_ff_1_q));  // open: nQ
  and and_1 (and_1_out, d_ff_1_q, xor_2_out);
  and and_2 (bob_one, bob, xor_3_out);
  and and_3 (bob_two, bob, xor_4_out);
  and and_4 (one_two, xor_3_out, xor_4_out);
  and and_5 (and_5_out, rd, wr);
  and and_6 (and_6_out, fw, bk);
  and and_7 (and_7_out, rd, bk);
  and and_8 (and_8_out, rd, fw);
  and and_9 (and_9_out, wr, bk);
  and and_10 (and_10_out, wr, fw);
  and and_11 (bob_one_two, bob_one, bob_two);
  or or_1 (or_1_out, and_5_out, and_6_out);
  or or_2 (or_2_out, and_7_out, and_8_out);
  or or_3 (or_3_out, and_9_out, and_10_out);
  or or_4 (or_4_out, bob_one_two, bob_one);
  or or_5 (or_5_out, bob_two, one_two);
  or or_6 (or_6_out, or_2_out, or_3_out);
  or or_7 (or_7_out, or_4_out, or_5_out);
  or or_8 (or_8_out, or_1_out, or_6_out);
  and and_12 (BOB_2, bob, nand_1_out);
  and and_13 (ONE_2, xor_3_out, nand_1_out);
  and and_14 (TWO_2, xor_4_out, nand_1_out);
  nand nand_1 (nand_1_out, or_7_out, or_7_out);
  and and_15 (halt, nand_1_out, or_8_out);
endmodule
